# Fritzing sketch AnalogInputPot (saved by Fritzing 0.9.3b)
circuit board: 6.88566cm x 5.36311cm
breadboards: 2

parts:
  LED2 = LED - 5mm [color="Red (633nm)" package="5 mm [THT]"]
  R1 = Rotary Potentiometer (Small) [maximum_resistance=100kΩ package=THT]
  Arduino2 = Arduino Uno (Rev3)

nets:
  N1: LED2.cathode, R1.leg1, Arduino2.GND
  N2: LED2.anode, Arduino2.D9_PWM
  N3: R1.wiper, Arduino2.A0
  N4: R1.leg2, Arduino2.5V

notes:
  Dans cet exemple, les valeurs du potentiomètre sont lues via des pins «Analog In». Les valeurs sont ensuite utilisées pour contrôler le taux de clignotement d'une LED. Exemple connexe: http://arduino.cc/en/Tutorial/AnalogInput
