# Fritzing sketch Blink1 (saved by Fritzing 0.9.3b)
breadboards: 1

parts:
  Composant1 = Arduino Uno (Rev3)
  LED1 = smd LED [color="Red (633nm)" package="1206 [SMD]"]
  R1 = Resistor [tolerance=±5% resistance=220 package=THT]

nets (from the breadboard view):
  N1: Composant1.D13/SCK, LED1.anode
  N2: Composant1.GND, R1.Pin_0
  N3: LED1.cathode, R1.Pin_1
