# Fritzing sketch LED_PWM (saved by Fritzing 0.9.3b)
breadboards: 1

parts:
  Part1 = Arduino Uno (Rev3)
  R1 = Resistor [tolerance=±5% resistance=220 package="0805 [SMD]"]
  LED1 = LED - 3mm [color="Red (633nm)" package="3 mm [THT]"]

nets:
  N1: Part1.D11_PWM/MOSI, LED1.anode
  N2: Part1.GND, R1.Pin_0
  N3: R1.Pin_1, LED1.cathode
