# Fritzing sketch AnalogInputPot1 (saved by Fritzing 0.9.3b)
breadboards: 1

parts:
  R2 = Rotary Potentiometer (Large) [maximum_resistance=100kΩ package=THT]
  Part1 = Arduino Uno (Rev3)
  LED1 = LED - 5mm [color="Red (633nm)" package="5 mm [THT]"]
  R3 = Resistor [tolerance=±5% resistance=220 package=THT]

nets:
  N1: R2.leg1, Part1.GND, R3.Pin_0
  N2: R2.wiper, Part1.A0
  N3: R2.leg2, Part1.5V
  N4: Part1.D11_PWM/MOSI, LED1.anode
  N5: LED1.cathode, R3.Pin_1
